// Logisim project logisim.circ as structural Verilog: 12 circuits, main circuit main
module main (
);

  ALU alu_1 ();  // open: Accumulator, Active, Control_Unit, BUS, Carry, Accumulator_2
endmodule

module ALU (
  input  [7:0] Accumulator,
  input  [7:0] BUS,
  input  Active,
  input  [2:0] Control_Unit,
  output Carry,
  output [7:0] Accumulator_2
);

  wire [7:0] Adder_output, And_Nand_output_acc_and, And_Nand_output_acc_nand, Inverter_output,
       multiplexer_1_out, Or_output_acc, shl_output_acc, shr_output_acc, Xor_output_acc;

  And_Nand And_Nand (
    .Input_Acc(Accumulator), .Input_Bus(BUS), .Output_Acc_AND(And_Nand_output_acc_and),
    .Output_Acc_NAND(And_Nand_output_acc_nand));
  Or Or (.Input_Acc(Accumulator), .Input_Bus(BUS), .Output_Acc(Or_output_acc));
  Xor Xor (.Input_Acc(Accumulator), .Input_Bus(BUS), .Output_Acc(Xor_output_acc));
  shl shl (.Input_Acc(Accumulator), .Output_Acc(shl_output_acc));
  shr shr (.Input_Acc(Accumulator), .Output_Acc(shr_output_acc));  // open: in_2
  Adder Adder (.Sub(Control_Unit[0]), .A(BUS), .B(Accumulator), .Output(Adder_output), .Carry(Carry));
  Inverter Inverter (.Input(Accumulator), .Output(Inverter_output));
  Multiplexer #(.select(3), .width(8), .enable("false")) multiplexer_1 (
    .in0(Adder_output), .in1(Adder_output), .in2(And_Nand_output_acc_nand), .in3(And_Nand_output_acc_and),
    .in4(Or_output_acc), .in5(Xor_output_acc), .in6(Inverter_output), .in7(shl_output_acc),
    .out(multiplexer_1_out), .sel(Control_Unit));
  assign Accumulator_2 = Active ? multiplexer_1_out : 8'bz;  // Controlled_Buffer controlled_buffer_1
endmodule

module Inverter (
  input  [7:0] Input,
  output [7:0] Output
);

  not not_1 (Output[0], Input[0]);
  not not_2 (Output[1], Input[1]);
  not not_3 (Output[2], Input[2]);
  not not_4 (Output[3], Input[3]);
  not not_5 (Output[4], Input[4]);
  not not_6 (Output[5], Input[5]);
  not not_7 (Output[6], Input[6]);
  not not_8 (Output[7], Input[7]);
endmodule

module Adder (
  input  Sub,
  input  [7:0] A,
  input  [7:0] B,
  output [7:0] Output,
  output Carry
);

  wire fulladder_1_carry_out, fulladder_2_carry_out, fulladder_3_carry_out, fulladder_4_carry_out,
       fulladder_5_carry_out, fulladder_6_carry_out, fulladder_7_carry_out, fulladder_8_carry_out, xor_1_out,
       xor_2_out, xor_3_out, xor_4_out, xor_5_out, xor_6_out, xor_7_out, xor_8_out;

  xor xor_1 (xor_1_out, B[0], Sub);
  xor xor_2 (xor_2_out, B[1], Sub);
  xor xor_3 (xor_3_out, B[2], Sub);
  xor xor_4 (xor_4_out, B[3], Sub);
  xor xor_5 (xor_5_out, B[4], Sub);
  xor xor_6 (xor_6_out, B[5], Sub);
  xor xor_7 (xor_7_out, B[6], Sub);
  xor xor_8 (xor_8_out, B[7], Sub);
  FullAdder fulladder_1 (.Carry_In(Sub), .A(A[0]), .B(xor_1_out), .Sum(Output[0]), .Carry_Out(fulladder_1_carry_out));
  FullAdder fulladder_2 (
    .Carry_In(fulladder_1_carry_out), .A(A[1]), .B(xor_2_out), .Sum(Output[1]),
    .Carry_Out(fulladder_2_carry_out));
  FullAdder fulladder_3 (
    .Carry_In(fulladder_2_carry_out), .A(A[2]), .B(xor_3_out), .Sum(Output[2]),
    .Carry_Out(fulladder_3_carry_out));
  FullAdder fulladder_4 (
    .Carry_In(fulladder_3_carry_out), .A(A[3]), .B(xor_4_out), .Sum(Output[3]),
    .Carry_Out(fulladder_4_carry_out));
  FullAdder fulladder_5 (
    .Carry_In(fulladder_4_carry_out), .A(A[4]), .B(xor_5_out), .Sum(Output[4]),
    .Carry_Out(fulladder_5_carry_out));
  FullAdder fulladder_6 (
    .Carry_In(fulladder_5_carry_out), .A(A[5]), .B(xor_6_out), .Sum(Output[5]),
    .Carry_Out(fulladder_6_carry_out));
  FullAdder fulladder_7 (
    .Carry_In(fulladder_6_carry_out), .A(A[6]), .B(xor_7_out), .Sum(Output[6]),
    .Carry_Out(fulladder_7_carry_out));
  FullAdder fulladder_8 (
    .Carry_In(fulladder_7_carry_out), .A(A[7]), .B(xor_8_out), .Sum(Output[7]),
    .Carry_Out(fulladder_8_carry_out));
  xor xor_9 (Carry, fulladder_8_carry_out, Sub);
endmodule

module FullAdder (
  input  Carry_In,
  input  A,
  input  B,
  output Sum,
  output Carry_Out
);

  wire halfadder_1_carry, halfadder_1_sum, halfadder_2_carry;

  HalfAdder halfadder_1 (.A(A), .B(B), .Sum(halfadder_1_sum), .Carry(halfadder_1_carry));
  HalfAdder halfadder_2 (.A(Carry_In), .B(halfadder_1_sum), .Sum(Sum), .Carry(halfadder_2_carry));
  or or_1 (Carry_Out, halfadder_2_carry, halfadder_1_carry);
endmodule

module HalfAdder (
  input  A,
  input  B,
  output Sum,
  output Carry
);

  xor xor_1 (Sum, A, B);
  and and_1 (Carry, A, B);
endmodule

module And_Nand (
  input  [7:0] Input_Acc,
  input  [7:0] Input_Bus,
  output [7:0] Output_Acc_AND,
  output [7:0] Output_Acc_NAND
);

  assign Output_Acc_AND = Input_Acc & Input_Bus;  // AND_Gate and_1, 8 bits wide
  assign Output_Acc_NAND = ~Output_Acc_AND;  // NOT_Gate not_1, 8 bits wide
endmodule

module Or (
  input  [7:0] Input_Acc,
  input  [7:0] Input_Bus,
  output [7:0] Output_Acc
);

  assign Output_Acc = Input_Acc | Input_Bus;  // OR_Gate or_1, 8 bits wide
endmodule

module Xor (
  input  [7:0] Input_Acc,
  input  [7:0] Input_Bus,
  output [7:0] Output_Acc
);

  assign Output_Acc = Input_Acc ^ Input_Bus;  // XOR_Gate xor_1, 8 bits wide
endmodule

module shl (
  input  [7:0] Input_Acc,
  output [7:0] Output_Acc
);

  assign Output_Acc = {Input_Acc[6:0], 1'b0};  // Buffer buffer_1, 8 bits wide
endmodule

module shr (
  input  [7:0] Input_Acc,
  input  in_2,
  output [7:0] Output_Acc
);

  wire [7:7] and_1_out;

  and and_1 (and_1_out[7], Input_Acc[7], in_2);
  assign Output_Acc = {and_1_out[7], Input_Acc[7:1]};  // Buffer buffer_1, 8 bits wide
endmodule

module Tests (
  input  [7:0] in_1,
  input  [7:0] in_2,
  output [7:0] out_3,
  output [7:0] out_4,
  output out_5,
  output [7:0] out_6,
  output [7:0] out_7
);

  Or or_1 (.Input_Acc(in_2), .Input_Bus(in_1), .Output_Acc(out_7));
  Inverter inverter_1 (.Input(8'hfe), .Output(out_3));
  Adder adder_1 (.Sub(1'b0), .A(8'h3), .B(8'hc), .Output(out_4), .Carry(out_5));
  Xor xor_1 (.Input_Acc(in_1), .Input_Bus(in_2), .Output_Acc(out_6));
endmodule
